# Fritzing sketch RaspberryWithDHT11 (saved by Fritzing 0.9.3b)

parts:
  Part1 = Arduino Uno (Rev3) - ICSP
  RHT1 = Humidity and Temperature Sensor RHT03

nets:
  N1: Part1.D2, RHT1.Data-signal
  5V: Part1.5V, RHT1.Vcc
  N2: Part1.GND, RHT1.GND_2
