# Fritzing sketch ChessWatchArduino2SSD1306DisplayTest (saved by Fritzing 0.9.3b)

parts:
  Part1 = Arduino Uno (Rev3) - ICSP
  Grove1 = Grove OLED 128x96
  S1 = Momentary Switch [package=ksa_sealed_tac_switch]

nets:
  N1: Part1.A4/SDA, Grove1.SCL
  N2: Part1.A5/SCL, Grove1.SDA
  N3: Part1.D8, S1.2
  GND: Part1.GND, Grove1.GND, S1.4
  5V: Part1.5V, Grove1.VCC
