# Fritzing sketch ChessWatchArduino2SSD1306Prototyp (saved by Fritzing 0.9.3b)

parts:
  Part1 = Arduino Uno (Rev3) - ICSP
  Grove1 = Grove OLED 128x96
  S1 = Momentary Switch [package=ksa_sealed_tac_switch]
  S2 = Momentary Switch [package=ksa_sealed_tac_switch]
  Grove2 = Grove OLED 128x96  # not connected

nets:
  N1: Part1.A4/SDA, Grove1.SCL
  N2: Part1.A5/SCL, Grove1.SDA
  N3: Part1.D8, S2.4
  N4: Part1.D9_PWM, S1.2
  5V: Part1.5V, Grove1.VCC
  GND: Part1.GND, Grove1.GND
