# Fritzing sketch retroJoyStickTester (saved by Fritzing 1.0.1rc)

parts:
  X1 = DB9 Connector [package=db9]
  Arduino_Uno = Arduino Uno (Rev3) - ICSP
  LED1_Fire = smd LED [color="Yellow (595nm)" package="0603 [SMD]"]
  LED2_Right = smd LED [color="Green (570nm)" package="0603 [SMD]"]
  LED3_Left = smd LED [color="Green (570nm)" package="0603 [SMD]"]
  LED4_Up = smd LED [color="Red (633nm)" package="0603 [SMD]"]
  R1 = Resistor [tolerance=±5% power=0.25W resistance=150 package=THT]
  R2 = Resistor [tolerance=±5% resistance=220 package="1206 [SMD]"]
  R3 = Resistor [tolerance=±5% power=0.25W resistance=150 package=THT]
  R4 = Resistor [tolerance=±5% power=0.25W resistance=220 package=THT]
  R5 = Resistor [tolerance=±5% power=0.25W resistance=150 package=THT]
  LED5_Down = smd LED [color="Red (633nm)" package="0603 [SMD]"]
  Oled_Display = Grove OLED 128x96

nets (from the breadboard view):
  N1: X1.1, Arduino_Uno.D4
  N2: X1.2, Arduino_Uno.D5_PWM
  N3: X1.3, Arduino_Uno.D6_PWM
  N4: X1.4, Arduino_Uno.D7
  N5: X1.5, Arduino_Uno.A0
  N6: X1.6, Arduino_Uno.D3_PWM
  5V: X1.7, Arduino_Uno.5V, Oled_Display.VCC
  GND: X1.8, Arduino_Uno.GND, R1.Pin_0, R2.Pin_0, R3.Pin_0, R4.Pin_0, R5.Pin_0, Oled_Display.GND
  N7: X1.9, Arduino_Uno.A1
  N8: Arduino_Uno.A4/SDA, Oled_Display.SDA
  N9: Arduino_Uno.D8, LED5_Down.anode
  N10: Arduino_Uno.D9_PWM, LED3_Left.anode
  N11: Arduino_Uno.D10_PWM/SS, LED2_Right.anode
  N12: Arduino_Uno.D11_PWM/MOSI, LED4_Up.anode
  N13: Arduino_Uno.D12/MISO, LED1_Fire.anode
  N14: Arduino_Uno.A5/SCL, Oled_Display.SCL
  N15: LED1_Fire.cathode, R1.Pin_1
  N16: LED2_Right.cathode, R5.Pin_1
  N17: LED3_Left.cathode, R3.Pin_1
  N18: LED4_Up.cathode, R4.Pin_1
  N19: R2.Pin_1, LED5_Down.cathode
