# Fritzing sketch UnoWithEncoderMotor (saved by Fritzing 0.9.3b)

parts:
  DC_Mot_Enc1 = DC Motor with two-phase hall-encoder [part_number=VT-E-G25A-06-177E]
  Part1 = Arduino Ethernet Shield (Rev3)

nets:
  N1: DC_Mot_Enc1.pin3, Part1.5V
  N2: DC_Mot_Enc1.pin4, Part1.GND
  N3: DC_Mot_Enc1.pin5, Part1.D2
  N4: DC_Mot_Enc1.pin6, Part1.A2
