# Fritzing sketch BH1750Sketch (saved by Fritzing 0.9.3b)

parts:
  Part2 = Arduino Uno (Rev3) - ICSP
  Part4 = BH1750

nets:
  N1: Part2.A4/SDA, Part4.SDA
  N2: Part2.A5/SCL, Part4.SCL
  5V: Part2.5V, Part4.VCC
  GND: Part2.GND, Part4.GND

custom parts:
  BH1750: Light Sensor
