# Fritzing sketch Untitled Sketch 2 (saved by Fritzing 1.0.1rc)

parts:
  Bauteil1 = Arduino Mega 2560 (Rev3)
  Bauteil2 = 16-Channel 12-bit PCA9685 PWM/Servo Driver
  J1 = Basic Servo
  R1 = 6mm Trimmer Potentiometer [maximum_resistance=10kΩ knob_status=50% power=0.5W package=THT]

nets:
  N1: Bauteil1.A0, R1.wiper
  N2: Bauteil1.D21/SCL, Bauteil1.SCL, Bauteil2.SCL
  N3: Bauteil1.D20/SDA, Bauteil1.SDA, Bauteil2.SDA
  5V: Bauteil1.5V, Bauteil2.V+, J1.vcc
  GND: Bauteil1.GND, Bauteil2.GND, J1.gnd
  VIN: Bauteil1.VIN, Bauteil2.VCC
  N4: Bauteil2.0, J1.pulse

custom parts:
  16-Channel 12-bit PCA9685 PWM/Servo Driver: The Adafruit 16-Channel 12-bit PWM/Servo Driver will drive up to 16 servos over I2C with only 2 pins. The on-board PCA9685 PWM controller will drive all 16 channels simultaneously with no additional processing overhead. What's more, you can chain up to 62 of them to control up to 992 servos - all with the same 2 pins
