# Fritzing sketch Rf2401SketchTest (saved by Fritzing 0.9.3b)

parts:
  Part1 = NRF24L01+ Breakout Board
  Part3 = Arduino Uno (Rev3) - ICSP
  Part4 = Arduino Uno (Rev3) - ICSP
  Part5 = NRF24L01+ Breakout Board

nets:
  GND: Part1.GND, Part3.GND
  VCC: Part1.VCC, Part3.3V3
  N1: Part1.CE, Part3.D9_PWM
  N2: Part1.CS, Part3.D10_PWM/SS
  N3: Part1.SCK, Part3.D13/SCK
  N4: Part1.MOSI, Part3.D11_PWM/MOSI
  N5: Part1.MISO, Part3.ICSP_MISO, Part3.D12/MISO
  N6: Part4.ICSP_MISO, Part4.D12/MISO, Part5.MISO
  N7: Part4.D9_PWM, Part5.CE
  N8: Part4.D10_PWM/SS, Part5.CS
  N9: Part4.D11_PWM/MOSI, Part5.MOSI
  N10: Part4.D13/SCK, Part5.SCK
  3V3: Part4.3V3, Part5.VCC
  GND_2: Part4.GND, Part5.GND
